// Logisim project first (2).circ as structural Verilog
module main (
  input  X1,
  input  X2,
  input  X3,
  output Bi,
  output Di
);

  wire and_1_out, and_2_out, and_3_out, and_4_out, and_5_out, not_1_out, not_2_out, not_3_out, or_1_out;

  not not_1 (not_1_out, X1);
  not not_2 (not_2_out, X2);
  not not_3 (not_3_out, X3);
  and and_1 (and_1_out, X2, X3);
  and and_2 (and_2_out, not_1_out, X3);
  and and_3 (and_3_out, not_1_out, X2);
  or or_1 (or_1_out, X1, not_2_out, not_3_out);
  and and_4 (and_4_out, X1, not_2_out, not_3_out);
  or or_2 (Di, and_5_out, and_4_out);
  or or_3 (Bi, and_1_out, and_2_out, and_3_out);
  and and_5 (and_5_out, Bi, or_1_out);
endmodule
