// Logisim project gray5 (2).circ as structural Verilog: 8 circuits, main circuit main
module main (
  input  [3:0] GrayBSD1,
  input  [3:0] GrayBSD2,
  output out_3,
  output out_4,
  output out_5,
  output out_6,
  output out_7,
  output out_8,
  output out_9,
  output out_10
);

  wire [3:0] binary_to_bcd_converter_1_p2, binary_to_bcd_converter_1_p3, graytobsd8421_1_d0,
       graytobsd8421_2_d0;
  wire [5:0] binary_to_bcd_converter_1_p1, bit_extender_1_out, bit_extender_2_out, bit_extender_3_out,
       sum6_1_out_3;

  GrayToBSD8421 graytobsd8421_1 (
    .g3(GrayBSD1[3]), .g2(GrayBSD1[2]), .g1(GrayBSD1[1]), .g0(GrayBSD1[0]), .d3(graytobsd8421_1_d0[3]),
    .d2(graytobsd8421_1_d0[2]), .d1(graytobsd8421_1_d0[1]), .d0(graytobsd8421_1_d0[0]));
  GrayToBSD8421 graytobsd8421_2 (
    .g3(GrayBSD2[3]), .g2(GrayBSD2[2]), .g1(GrayBSD2[1]), .g0(GrayBSD2[0]), .d3(graytobsd8421_2_d0[3]),
    .d2(graytobsd8421_2_d0[2]), .d1(graytobsd8421_2_d0[1]), .d0(graytobsd8421_2_d0[0]));
  assign bit_extender_1_out = {{2{1'b0}}, graytobsd8421_1_d0};  // Bit_Extender bit_extender_1
  assign bit_extender_2_out = {{2{1'b0}}, graytobsd8421_2_d0};  // Bit_Extender bit_extender_2
  // Binary_to_BCD_converter #(.binvalue(6)) binary_to_bcd_converter_1: pin names not known; wires that end beside it: binary_to_bcd_converter_1_p1, binary_to_bcd_converter_1_p2, binary_to_bcd_converter_1_p3
  sum6 sum6_1 (.in_1(bit_extender_1_out), .in_2(bit_extender_2_out), .out_3(sum6_1_out_3));
  assign bit_extender_3_out = {{3{1'b0}}, 3'b101};  // Bit_Extender bit_extender_3
  sum6 sum6_2 (.in_1(sum6_1_out_3), .in_2(bit_extender_3_out), .out_3(binary_to_bcd_converter_1_p1));
  BSD8421ToGray bsd8421togray_1 (
    .d3(binary_to_bcd_converter_1_p3[3]), .d2(binary_to_bcd_converter_1_p3[2]),
    .d1(binary_to_bcd_converter_1_p3[1]), .d0(binary_to_bcd_converter_1_p3[0]), .g3(out_3), .g2(out_4),
    .g1(out_5), .g0(out_6));
  BSD8421ToGray bsd8421togray_2 (
    .d3(binary_to_bcd_converter_1_p2[3]), .d2(binary_to_bcd_converter_1_p2[2]),
    .d1(binary_to_bcd_converter_1_p2[1]), .d0(binary_to_bcd_converter_1_p2[0]), .g3(out_7), .g2(out_8),
    .g1(out_9), .g0(out_10));
endmodule

module BSD8421ToGray (
  input  d3,
  input  d2,
  input  d1,
  input  d0,
  output g3,
  output g2,
  output g1,
  output g0
);

  wire [1:0] bit_extender_1_out;
  wire [3:0] shifter_1_out;

  Shifter #(.shift("lr"), .width(4)) shifter_1 (
    .in({d3, d2, d1, d0}), .\dist (bit_extender_1_out), .out(shifter_1_out));
  assign bit_extender_1_out = {{1{1'b0}}, 1'b1};  // Bit_Extender bit_extender_1
  xor xor_1 (g0, shifter_1_out[0], d0);
  xor xor_2 (g1, shifter_1_out[1], d1);
  xor xor_3 (g2, shifter_1_out[2], d2);
  xor xor_4 (g3, shifter_1_out[3], d3);
endmodule

module GrayToBSD8421 (
  input  g3,
  input  g2,
  input  g1,
  input  g0,
  output d3,
  output d2,
  output d1,
  output d0
);

  xor xor_1 (d2, g2, g3);
  xor xor_2 (d1, g1, d2);
  xor xor_3 (d0, g0, d1);

  assign d3 = g3;
endmodule

module sum6 (
  input  [5:0] in_1,
  input  [5:0] in_2,
  output [5:0] out_3
);

  wire sum1_1_cout, sum1_2_cout, sum1_3_cout, sum1_4_cout, sum1_5_cout;

  sum1 sum1_1 (.x1(in_1[0]), .x2(in_2[0]), .x3(1'b0), .sum(out_3[0]), .cout(sum1_1_cout));
  sum1 sum1_2 (.x1(in_1[1]), .x2(in_2[1]), .x3(sum1_1_cout), .sum(out_3[1]), .cout(sum1_2_cout));
  sum1 sum1_3 (.x1(in_1[2]), .x2(in_2[2]), .x3(sum1_2_cout), .sum(out_3[2]), .cout(sum1_3_cout));
  sum1 sum1_4 (.x1(in_1[3]), .x2(in_2[3]), .x3(sum1_3_cout), .sum(out_3[3]), .cout(sum1_4_cout));
  sum1 sum1_5 (.x1(in_1[4]), .x2(in_2[4]), .x3(sum1_4_cout), .sum(out_3[4]), .cout(sum1_5_cout));
  sum1 sum1_6 (.x1(in_1[5]), .x2(in_2[5]), .x3(sum1_5_cout), .sum(out_3[5]));  // open: cout
endmodule

module sum1 (
  input  x1,
  input  x2,
  input  x3,
  output sum,
  output cout
);

  wire and_1_out, and_2_out, xor_1_out;

  xor xor_1 (xor_1_out, x1, x2);
  and and_1 (and_1_out, x3, xor_1_out);
  and and_2 (and_2_out, x1, x2);
  xor xor_2 (sum, xor_1_out, x3);
  or or_1 (cout, and_1_out, and_2_out);
endmodule

module sum8 (
  input  [7:0] in_1,
  input  [7:0] in_2,
  output [8:0] out_3
);

  wire sum1_1_cout, sum1_2_cout, sum1_3_cout, sum1_4_cout, sum1_5_cout, sum1_6_cout, sum1_7_cout;

  sum1 sum1_1 (.x1(in_1[0]), .x2(in_2[0]), .x3(1'b0), .sum(out_3[0]), .cout(sum1_1_cout));
  sum1 sum1_2 (.x1(in_1[1]), .x2(in_2[1]), .x3(sum1_1_cout), .sum(out_3[1]), .cout(sum1_2_cout));
  sum1 sum1_3 (.x1(in_1[2]), .x2(in_2[2]), .x3(sum1_2_cout), .sum(out_3[2]), .cout(sum1_3_cout));
  sum1 sum1_4 (.x1(in_1[3]), .x2(in_2[3]), .x3(sum1_3_cout), .sum(out_3[3]), .cout(sum1_4_cout));
  sum1 sum1_5 (.x1(in_1[4]), .x2(in_2[4]), .x3(sum1_4_cout), .sum(out_3[4]), .cout(sum1_5_cout));
  sum1 sum1_6 (.x1(in_1[5]), .x2(in_2[5]), .x3(sum1_5_cout), .sum(out_3[5]), .cout(sum1_6_cout));
  sum1 sum1_7 (.x1(in_1[6]), .x2(in_2[6]), .x3(sum1_6_cout), .sum(out_3[6]), .cout(sum1_7_cout));
  sum1 sum1_8 (.x1(in_1[7]), .x2(in_2[7]), .x3(sum1_7_cout), .sum(out_3[7]), .cout(out_3[8]));
endmodule

module sub (
  input  X1,
  input  X2,
  input  X3,
  output Bi,
  output Di
);

  wire and_1_out, and_2_out, and_3_out, and_4_out, and_5_out, not_1_out, not_2_out, not_3_out, or_1_out;

  not not_1 (not_1_out, X1);
  not not_2 (not_2_out, X2);
  not not_3 (not_3_out, X3);
  and and_1 (and_1_out, X2, X3);
  and and_2 (and_2_out, not_1_out, X3);
  and and_3 (and_3_out, not_1_out, X2);
  or or_1 (or_1_out, X1, not_2_out, not_3_out);
  and and_4 (and_4_out, X1, not_2_out, not_3_out);
  or or_2 (Bi, and_1_out, and_2_out, and_3_out);
  and and_5 (and_5_out, Bi, or_1_out);
  or or_3 (Di, and_5_out, and_4_out);
endmodule

module sub8 (
  input  [7:0] in_1,
  input  [7:0] in_2,
  output [8:0] out_3
);

  wire sub_1_bi, sub_2_bi, sub_3_bi, sub_4_bi, sub_5_bi, sub_6_bi, sub_7_bi;

  sub sub_1 (.X1(in_1[0]), .X2(in_2[0]), .X3(1'b0), .Bi(sub_1_bi), .Di(out_3[0]));
  sub sub_2 (.X1(in_1[1]), .X2(in_2[1]), .X3(sub_1_bi), .Bi(sub_2_bi), .Di(out_3[1]));
  sub sub_3 (.X1(in_1[2]), .X2(in_2[2]), .X3(sub_2_bi), .Bi(sub_3_bi), .Di(out_3[2]));
  sub sub_4 (.X1(in_1[3]), .X2(in_2[3]), .X3(sub_3_bi), .Bi(sub_4_bi), .Di(out_3[3]));
  sub sub_5 (.X1(in_1[4]), .X2(in_2[4]), .X3(sub_4_bi), .Bi(sub_5_bi), .Di(out_3[4]));
  sub sub_6 (.X1(in_1[5]), .X2(in_2[5]), .X3(sub_5_bi), .Bi(sub_6_bi), .Di(out_3[5]));
  sub sub_7 (.X1(in_1[6]), .X2(in_2[6]), .X3(sub_6_bi), .Bi(sub_7_bi), .Di(out_3[6]));
  sub sub_8 (.X1(in_1[7]), .X2(in_2[7]), .X3(sub_7_bi), .Bi(out_3[8]), .Di(out_3[7]));
endmodule
