// Logisim project third (2).circ as structural Verilog: 1 circuit, main circuit main
module main (
  output out_1,
  output out_2,
  output out_3,
  output out_4
);

  wire and_1_out, and_2_out, clock_1_out, not_1_out, not_2_out, not_3_out;

  Clock clock_1 (.out(clock_1_out));
  and and_1 (and_1_out, not_2_out, not_3_out, not_1_out);
  not not_1 (not_1_out, out_2);
  T_Flip_Flop t_ff_1 (.T(and_1_out), .clk(clock_1_out), .Q(out_1));  // open: Qn, reset, preset
  T_Flip_Flop t_ff_2 (.T(and_2_out), .clk(clock_1_out), .Q(out_2));  // open: Qn, reset, preset
  and and_2 (and_2_out, not_2_out, not_3_out);
  not not_2 (not_2_out, out_4);
  not not_3 (not_3_out, out_3);
  T_Flip_Flop t_ff_3 (.T(not_2_out), .clk(clock_1_out), .Q(out_3));  // open: Qn, reset, preset
  T_Flip_Flop t_ff_4 (.T(1'b1), .clk(clock_1_out), .Q(out_4));  // open: Qn, reset, preset
endmodule
